# Fritzing sketch Brouwerij (saved by Fritzing 0.9.3b)
circuit board: 7.587cm x 5.33677cm
breadboards: 1

parts:
  Pi1 = Adafruit Pi Cobbler
  R1 = Resistor [tolerance=±5% resistance=4.7k part_number=pullup package=THT]
  Q1 = NPN-Transistor [package="TO92 [THT]"]
  R2 = Resistor [tolerance=±5% resistance=1k package=THT]
  J2 = Power plug [part_number="to SSR"]
  J1 = screw terminal, 3 pins [part_number="to DS18B20"]

nets:
  N1: Pi1.3V3, R1.Pin_0, J1.pin1
  +5V: Pi1.5V0, J2.VCC
  GND: Pi1.GND, Q1.E, J1.pin3
  N2: Pi1.#4, R1.Pin_1, J1.pin2
  N3: Pi1.#17, R2.Pin_0
  N4: Q1.B, R2.Pin_1
  N5: Q1.C, J2.GND

notes:
  DS18B20:
  1. GND (white)
  2. DQ (blue/white)
  3. VDD (orange/white)
  Brewgear π, Home brewery automation, 1
  Connection to SSR

custom parts:
  Adafruit Pi Cobbler: Adafruit Pi Cobbler GPIO Breakout for Raspberry Pi
